// Logisim project PC.circ as structural Verilog: 1 circuit, main circuit main
module main (
  input  Start,
  input  x0___x1,
  input  Reset,
  input  Clock,
  input  y0___y1,
  input  dx___dy
);

  wire [3:0] multiplexer_1_out, multiplexer_2_out, multiplexer_3_out, multiplexer_4_out, multiplexer_5_out,
       multiplexer_6_out, register_1_q;

  Multiplexer #(.width(4)) multiplexer_1 (
    .in0(4'b0000), .in1(4'b0001), .out(multiplexer_1_out), .sel(Start));  // open: en
  Multiplexer #(.width(4)) multiplexer_2 (
    .in0(4'b0011), .in1(4'b0100), .out(multiplexer_2_out), .sel(x0___x1));  // open: en
  Multiplexer #(.width(4)) multiplexer_3 (
    .in0(4'b0101), .in1(4'b0110), .out(multiplexer_3_out), .sel(y0___y1));  // open: en
  Multiplexer #(.width(4)) multiplexer_4 (
    .in0(4'b0111), .in1(4'b1000), .out(multiplexer_4_out), .sel(dx___dy));  // open: en
  Multiplexer #(.select(4), .width(4)) multiplexer_5 (
    .in0(multiplexer_1_out), .in1(4'b0010), .in2(multiplexer_2_out), .in3(multiplexer_3_out),
    .in4(multiplexer_3_out), .in5(multiplexer_4_out), .in6(multiplexer_4_out), .out(multiplexer_5_out),
    .sel(register_1_q));  // open: in7, in8, in9, in10, in11, in12, in13, in14, in15, en
  Multiplexer #(.width(4)) multiplexer_6 (
    .in0(multiplexer_5_out), .in1(4'b0000), .out(multiplexer_6_out), .sel(Reset));  // open: en
  Register #(.width(4)) register_1 (.D(multiplexer_6_out), .en(1'b1), .Q(register_1_q), .clk(Clock));  // open: clr

  // Notes on the sheet:
  //   E0
  //   E1
  //   E3
  //   E4
  //   E5
  //   E6
  //   E7
  //   E8
  //   E2
  //   E0
endmodule
