// Logisim project PO.circ as structural Verilog: 2 circuits, main circuit PO
module PO (
  input  Sel_y0,
  input  [31:0] Param_y0,
  input  Load_y0,
  input  Sel_x0,
  input  Start,
  input  [31:0] Param_x0,
  input  Load_x0,
  input  [31:0] Param_x1,
  input  Load_dx,
  input  Clock,
  input  [31:0] Param_y1,
  input  Load_dy,
  input  Sel_sx,
  input  Load_sx,
  input  Sel_sy,
  input  Load_sy,
  input  [1:0] Sel_err,
  input  Load_err,
  input  Load_e2,
  output x0____x1____y0____y1,
  output x0___x1,
  output y0___y1,
  output dx___dy,
  output e2____dx,
  output e2___dy
);

  wire comparator_1_eq, comparator_2_eq, or_1_out, or_2_out;
  wire [31:0] abs_2_return_n, abs_return_n, adder_1_out, adder_2_out, adder_3_out, divider_1_out,
       divider_2_out, dx_q, e2_q, err_q, multiplexer_1_out, multiplexer_2_out, multiplexer_3_out,
       multiplexer_4_out, multiplexer_5_out, multiplier_1_out, multiplier_2_out, subtractor_1_out,
       subtractor_2_out, subtractor_3_out, sx_q, sy_q, x0_q, y0_q;

  Multiplier #(.width(32)) multiplier_1 (.a(dx_q), .b({32{1'b1}}), .out(multiplier_1_out));  // open: cin, cout
  Adder #(.width(32)) adder_1 (.a(Param_y0), .b(sy_q), .out(adder_1_out));  // open: cin, cout
  Adder #(.width(32)) adder_2 (.a(Param_x0), .b(sx_q), .out(adder_2_out));  // open: cin, cout
  Subtractor #(.width(32)) subtractor_1 (.a(Param_x1), .b(x0_q), .out(subtractor_1_out));  // open: bin, bout
  Subtractor #(.width(32)) subtractor_2 (.a(Param_y1), .b(y0_q), .out(subtractor_2_out));  // open: bin, bout
  Divider #(.width(32)) divider_1 (.a(dx_q), .b(32'h2), .out(divider_1_out));  // open: upper, rem
  Divider #(.width(32)) divider_2 (.a(multiplier_1_out), .b(32'h2), .out(divider_2_out));  // open: upper, rem
  Subtractor #(.width(32)) subtractor_3 (.a(err_q), .b(dx_q), .out(subtractor_3_out));  // open: bin, bout
  Adder #(.width(32)) adder_3 (.a(err_q), .b(dx_q), .out(adder_3_out));  // open: cin, cout
  Multiplexer #(.width(32)) multiplexer_1 (
    .in0(Param_y0), .in1(adder_1_out), .out(multiplexer_1_out), .sel(Sel_y0));  // open: en
  Register #(.width(32)) y0 (.D(multiplexer_1_out), .en(or_1_out), .Q(y0_q), .clk(Clock));  // open: clr
  Register #(.width(32)) x0 (.D(multiplexer_2_out), .en(or_2_out), .Q(x0_q), .clk(Clock));  // open: clr
  Multiplexer #(.width(32)) multiplexer_2 (
    .in0(Param_x0), .in1(adder_2_out), .out(multiplexer_2_out), .sel(Sel_x0));  // open: en
  Register #(.width(32)) dx (.D(abs_return_n), .en(Load_dx), .Q(dx_q), .clk(Clock));  // open: clr
  abs abs (.Param_N(subtractor_1_out), .Return_N(abs_return_n));
  Register #(.width(32)) dy (.D(abs_2_return_n), .en(Load_dy), .Q(dx_q), .clk(Clock));  // open: clr
  abs abs_2 (.Param_N(subtractor_2_out), .Return_N(abs_2_return_n));
  Register #(.width(32)) sx (.D(multiplexer_3_out), .en(Load_sx), .Q(sx_q), .clk(Clock));  // open: clr
  Multiplexer #(.width(32)) multiplexer_3 (
    .in0(32'h1), .in1({32{1'b1}}), .out(multiplexer_3_out), .sel(Sel_sx));  // open: en
  Multiplexer #(.width(32)) multiplexer_4 (
    .in0(32'h1), .in1({32{1'b1}}), .out(multiplexer_4_out), .sel(Sel_sy));  // open: en
  Register #(.width(32)) sy (.D(multiplexer_4_out), .en(Load_sy), .Q(sy_q), .clk(Clock));  // open: clr
  Multiplexer #(.select(2), .width(32)) multiplexer_5 (
    .in0(divider_1_out), .in1(divider_2_out), .in2(subtractor_3_out), .in3(adder_3_out),
    .out(multiplexer_5_out), .sel(Sel_err));  // open: en
  Register #(.width(32)) err (.D(multiplexer_5_out), .en(Load_err), .Q(err_q), .clk(Clock));  // open: clr
  Register #(.width(32)) e2 (.D(err_q), .en(Load_e2), .Q(e2_q), .clk(Clock));  // open: clr
  or or_1 (or_1_out, Load_y0, Start);
  or or_2 (or_2_out, Start, Load_x0);
  Comparator #(.width(32)) comparator_1 (.a(Param_y1), .b(y0_q), .eq(comparator_1_eq));  // open: gt, lt
  Comparator #(.width(32)) comparator_2 (.a(x0_q), .b(Param_x1), .eq(comparator_2_eq));  // open: gt, lt
  Comparator #(.width(32)) comparator_3 (.a(x0_q), .b(Param_x1), .lt(x0___x1));  // open: gt, eq
  Comparator #(.width(32)) comparator_4 (.a(y0_q), .b(Param_y1), .lt(y0___y1));  // open: gt, eq
  Comparator #(.width(32)) comparator_5 (.a(dx_q), .b(dx_q), .gt(dx___dy));  // open: eq, lt
  Multiplier #(.width(32)) multiplier_2 (.a(dx_q), .b({32{1'b1}}), .out(multiplier_2_out));  // open: cin, cout
  Comparator #(.width(32)) comparator_6 (.a(e2_q), .b(multiplier_2_out), .gt(e2____dx));  // open: eq, lt
  Comparator #(.width(32)) comparator_7 (.a(e2_q), .b(dx_q), .lt(e2___dy));  // open: gt, eq
  and and_1 (x0____x1____y0____y1, comparator_1_eq, comparator_2_eq);
endmodule

module abs (
  input  [31:0] Param_N,
  output [31:0] Return_N
);

  wire comparator_1_lt;
  wire [31:0] multiplier_1_out;

  Multiplier #(.width(32)) multiplier_1 (.a(Param_N), .b({32{1'b1}}), .out(multiplier_1_out));  // open: cin, cout
  Comparator #(.width(32)) comparator_1 (.a(Param_N), .b({32{1'b0}}), .lt(comparator_1_lt));  // open: gt, eq
  Multiplexer #(.width(32)) multiplexer_1 (
    .in0(Param_N), .in1(multiplier_1_out), .out(Return_N), .sel(comparator_1_lt));  // open: en
endmodule
