// Logisim project abs.circ as structural Verilog: 1 circuit, main circuit main
module main (
  input  [31:0] Param_N,
  output [31:0] Return_N
);

  wire comparator_1_lt;
  wire [31:0] multiplier_1_out;

  Multiplier #(.width(32)) multiplier_1 (.a(Param_N), .b({32{1'b1}}), .out(multiplier_1_out));  // open: cin, cout
  Comparator #(.width(32)) comparator_1 (.a(Param_N), .b({32{1'b0}}), .lt(comparator_1_lt));  // open: gt, eq
  Multiplexer #(.width(32)) multiplexer_1 (
    .in0(Param_N), .in1(multiplier_1_out), .out(Return_N), .sel(comparator_1_lt));  // open: en
endmodule
